# Fritzing sketch Diagrama_Electromecánico_PIPO (saved by Fritzing 0.9.3b)

parts:
  Componente1 = Arduino Nano (Rev3.0)
  M1 = DC Motor
  BAT1 = BC9VPC [package=bc9vpc]
  S1 = Round Pushbutton
  S2 = H-Bridge with L298N
  M3 = DC Motor
  S3 = H-Bridge with L298N
  M4 = DC Motor
  U1 = XBEE-1 [package=xbee-1_lock]
  Componente2 = pinocc.io protoboard

nets:
  N1: Componente1.D1/TX, U1.DIO4
  N2: Componente1.D0/RX, U1.GND
  N3: Componente1.D6, S2.IN2
  N4: Componente1.D7, S2.IN1
  N5: Componente1.D8, S3.IN4
  N6: Componente1.D9, S3.IN3
  N7: Componente1.D10, S3.IN2
  N8: Componente1.D11/MOSI, S3.IN1
  N9: M1.pin_1, S3.OUT1-Motor1
  N10: M1.pin_2, S3.OUT2-Motor1
  N11: BAT1.V-, S1.leg1
  N12: S2.OUT1-Motor1, M3.pin_1
  N13: S2.OUT2-Motor1, M3.pin_2
  N14: S3.OUT3-Motor2, M4.pin_2
  N15: S3.OUT4-Motor2, M4.pin_1
  N16: Componente2.13, Componente2.38
  N17: Componente2.20, Componente2.60

notes:
  Regulador de voltaje
  12V a 9V
  Batería de 12V

custom parts:
  H-Bridge with L298N: h-bridge
